// Logisim project NanoSwitch16.circ as structural Verilog: 2 circuits, main circuit main
module main (
  input  [3:0] in_1,
  input  [3:0] in_2,
  output _0100,
  output _0101,
  output _0110,
  output _0111,
  output _1000,
  output _1001,
  output _1010
);

  wire adder_1_y, adder_2_x, adder_2_y, adder_3_x, adder_3_y, adder_4_x, adder_4_y, adder_5_x, adder_5_y,
       adder_6_x, adder_6_y, adder_7_x, adder_8_x, adder_8_y, adder_9_x, adder_9_y, adder_10_x, adder_10_y,
       adder_11_x, adder_11_y, and_1_out, and_2_out, and_3_out, and_4_out, and_5_out, and_6_out, and_7_out,
       and_8_out, and_9_out, and_10_out, and_11_out, and_12_out, and_13_out, and_14_out, and_15_out,
       and_16_out, and_17_out, and_18_out, and_19_out, and_20_out, and_21_out, and_22_out, and_23_out,
       and_24_out, and_25_out, and_26_out, and_27_out, and_28_out, and_29_out, and_30_out, and_31_out,
       and_32_out, and_33_out, and_34_out, and_35_out, and_36_out, and_37_out, and_38_out, and_39_out,
       and_40_out, and_41_out, and_42_out, and_43_out, and_44_out, and_45_out, and_46_out, and_47_out,
       and_48_out, and_49_out, and_50_out, and_51_out, and_52_out, and_53_out, and_54_out, and_55_out,
       and_56_out, and_57_out, and_58_out, and_59_out, and_60_out, and_61_out, and_62_out, and_63_out,
       and_64_out, and_65_out, and_66_out, and_67_out, and_68_out, and_69_out, and_70_out, and_71_out,
       and_79_out, clock_1_out, d_ff_1_qn, d_ff_2_q, d_ff_3_q, d_ff_8_q, d_ff_8_qn, d_ff_13_q, d_ff_14_q,
       d_ff_15_q, d_ff_16_q, d_ff_17_q, d_ff_18_q, d_ff_19_q, d_ff_20_q, execute_puls_out, fetch, not_1_out,
       not_2_out, not_3_out, not_4_out, not_5_out, not_6_out, not_7_out, not_8_out, not_9_out, not_10_out,
       not_11_out, not_12_out, not_13_out, not_14_out, not_15_out, or_1_out, or_6_out, or_7_out, or_8_out,
       or_9_out, or_10_out, or_19_out, or_20_out;
  wire [3:0] adder_7_y, d_ff_7_q, d_ff_9_q, d_ff_21_q, or_2_out, or_21_out, or_30_out;
  wire [7:0] or_11_out, or_36_out, ram_1_dout;

  Clock clock_1 (.out(clock_1_out));
  and execute_puls (execute_puls_out, clock_1_out, fetch);
  not not_1 (not_1_out, fetch);
  not not_2 (not_2_out, clock_1_out);
  and and_1 (and_1_out, fetch, and_70_out);
  not not_3 (not_3_out, clock_1_out);
  or or_1 (or_1_out, and_71_out, and_69_out);
  D_Flip_Flop d_ff_1 (.D(not_1_out), .clk(not_2_out), .Q(fetch), .Qn(d_ff_1_qn));  // open: preset, reset
  D_Flip_Flop d_ff_2 (.D(and_1_out), .clk(not_3_out), .Q(d_ff_2_q));  // open: Qn, preset, reset
  D_Flip_Flop d_ff_3 (.D(and_2_out), .clk(not_4_out), .Q(d_ff_3_q));  // open: Qn, preset, reset
  and and_2 (and_2_out, fetch, or_1_out);
  not not_4 (not_4_out, clock_1_out);
  and and_3 (and_3_out, or_11_out[4], d_ff_8_q);
  and and_4 (and_4_out, or_11_out[5], d_ff_8_q);
  and and_5 (and_5_out, or_11_out[6], d_ff_8_q);
  and and_6 (and_6_out, or_11_out[7], d_ff_8_q);
  D_Flip_Flop d_ff_4 (.D(d_ff_13_q), .clk(d_ff_1_qn), .Q(d_ff_7_q[3]));  // open: Qn, preset, reset
  D_Flip_Flop d_ff_5 (.D(d_ff_14_q), .clk(d_ff_1_qn), .Q(d_ff_7_q[2]));  // open: Qn, preset, reset
  D_Flip_Flop d_ff_6 (.D(d_ff_15_q), .clk(d_ff_1_qn), .Q(d_ff_7_q[1]));  // open: Qn, preset, reset
  D_Flip_Flop d_ff_7 (.D(d_ff_16_q), .clk(d_ff_1_qn), .Q(d_ff_7_q[0]));  // open: Qn, preset, reset
  not not_5 (not_5_out, and_70_out);
  and and_7 (and_7_out, in_1[0], fetch);
  and and_8 (and_8_out, in_1[1], fetch);
  and and_9 (and_9_out, in_1[2], fetch);
  and and_10 (and_10_out, in_1[3], fetch);
  and and_11 (and_11_out, in_2[0], d_ff_1_qn);
  and and_12 (and_12_out, in_2[1], d_ff_1_qn);
  and and_13 (and_13_out, in_2[2], d_ff_1_qn);
  and and_14 (and_14_out, in_2[3], d_ff_1_qn);
  and and_15 (and_15_out, or_11_out[0], d_ff_8_qn);
  and and_16 (and_16_out, or_11_out[1], d_ff_8_qn);
  and and_17 (and_17_out, or_11_out[2], d_ff_8_qn);
  and and_18 (and_18_out, or_11_out[3], d_ff_8_qn);
  and and_19 (and_19_out, fetch, not_5_out);
  and and_20 (and_20_out, clock_1_out, not_6_out);
  not not_6 (not_6_out, and_1_out);
  or or_2 (or_2_out[0], and_7_out, and_11_out);
  or or_3 (or_2_out[1], and_8_out, and_12_out);
  or or_4 (or_2_out[2], and_9_out, and_13_out);
  or or_5 (or_2_out[3], and_10_out, and_14_out);
  RAM ram_1 (
    .addr({or_2_out, or_21_out}), .we(d_ff_2_q), .oe(not_7_out), .clk(or_6_out), .din(or_36_out),
    .dout(ram_1_dout));
  not not_7 (not_7_out, d_ff_2_q);
  or or_6 (or_6_out, and_20_out, d_ff_2_q);
  D_Flip_Flop d_ff_8 (.Q(d_ff_8_q), .Qn(d_ff_8_qn));  // open: D, clk, preset, reset
  D_Flip_Flop d_ff_9 (.D(or_7_out), .clk(d_ff_3_q), .Q(d_ff_9_q[0]));  // open: Qn, preset, reset
  or or_7 (or_7_out, and_15_out, and_3_out);
  D_Flip_Flop d_ff_10 (.D(or_8_out), .clk(d_ff_3_q), .Q(d_ff_9_q[1]));  // open: Qn, preset, reset
  or or_8 (or_8_out, and_16_out, and_4_out);
  D_Flip_Flop d_ff_11 (.D(or_9_out), .clk(d_ff_3_q), .Q(d_ff_9_q[2]));  // open: Qn, preset, reset
  or or_9 (or_9_out, and_17_out, and_5_out);
  D_Flip_Flop d_ff_12 (.D(or_10_out), .clk(d_ff_3_q), .Q(d_ff_9_q[3]));  // open: Qn, preset, reset
  or or_10 (or_10_out, and_18_out, and_6_out);
  adder adder_1 (.a(d_ff_7_q[3]), .b(adder_2_x), .y(adder_1_y));  // open: x
  adder adder_2 (.a(d_ff_7_q[2]), .b(adder_3_x), .x(adder_2_x), .y(adder_2_y));
  adder adder_3 (.a(d_ff_7_q[1]), .b(adder_4_x), .x(adder_3_x), .y(adder_3_y));
  adder adder_4 (.a(d_ff_7_q[0]), .b(1'b1), .x(adder_4_x), .y(adder_4_y));
  not not_8 (not_8_out, clock_1_out);
  or or_11 (or_11_out[0], and_22_out, and_26_out);
  or or_12 (or_11_out[1], and_23_out, and_27_out);
  or or_13 (or_11_out[2], and_24_out, and_28_out);
  or or_14 (or_11_out[3], and_25_out, and_29_out);
  or or_15 (or_11_out[4], and_22_out, and_30_out);
  or or_16 (or_11_out[5], and_23_out, and_31_out);
  or or_17 (or_11_out[6], and_24_out, and_32_out);
  or or_18 (or_11_out[7], and_25_out, and_33_out);
  not not_9 (not_9_out, and_71_out);
  D_Flip_Flop d_ff_13 (.D(adder_1_y), .clk(clock_1_out), .Q(d_ff_13_q));  // open: Qn, preset, reset
  D_Flip_Flop d_ff_14 (.D(adder_2_y), .clk(clock_1_out), .Q(d_ff_14_q));  // open: Qn, preset, reset
  D_Flip_Flop d_ff_15 (.D(adder_3_y), .clk(clock_1_out), .Q(d_ff_15_q));  // open: Qn, preset, reset
  D_Flip_Flop d_ff_16 (.D(adder_4_y), .clk(clock_1_out), .Q(d_ff_16_q));  // open: Qn, preset, reset
  and and_21 (and_21_out, and_19_out, not_8_out);
  and and_22 (and_22_out, adder_7_y[0], and_71_out);
  and and_23 (and_23_out, adder_7_y[1], and_71_out);
  and and_24 (and_24_out, adder_7_y[2], and_71_out);
  and and_25 (and_25_out, adder_7_y[3], and_71_out);
  and and_26 (and_26_out, ram_1_dout[0], not_10_out);
  and and_27 (and_27_out, ram_1_dout[1], not_10_out);
  and and_28 (and_28_out, ram_1_dout[2], not_10_out);
  and and_29 (and_29_out, ram_1_dout[3], not_10_out);
  and and_30 (and_30_out, ram_1_dout[4], not_10_out);
  and and_31 (and_31_out, ram_1_dout[5], not_10_out);
  and and_32 (and_32_out, ram_1_dout[6], not_10_out);
  and and_33 (and_33_out, ram_1_dout[7], not_10_out);
  and and_34 (and_34_out, not_9_out, d_ff_8_q);
  and and_35 (and_35_out, not_9_out, d_ff_8_qn);
  and and_36 (and_36_out, and_71_out, d_ff_8_qn);
  or or_19 (or_19_out, and_35_out, and_37_out);
  and and_37 (and_37_out, and_71_out, d_ff_8_q);
  not not_10 (not_10_out, and_71_out);
  or or_20 (or_20_out, and_34_out, and_36_out);
  and and_38 (and_38_out, ram_1_dout[4], or_19_out);
  and and_39 (and_39_out, ram_1_dout[5], or_19_out);
  and and_40 (and_40_out, ram_1_dout[6], or_19_out);
  and and_41 (and_41_out, ram_1_dout[7], or_19_out);
  or or_21 (or_21_out[0], and_49_out, and_53_out);
  or or_22 (or_21_out[1], and_50_out, and_54_out);
  or or_23 (or_21_out[2], and_51_out, and_55_out);
  or or_24 (or_21_out[3], and_52_out, and_56_out);
  or or_25 (or_36_out[7], and_42_out, and_62_out);
  and and_42 (and_42_out, or_20_out, d_ff_9_q[3]);
  D_Flip_Flop d_ff_17 (.D(ram_1_dout[4]), .clk(and_21_out), .Q(d_ff_17_q));  // open: Qn, preset, reset
  D_Flip_Flop d_ff_18 (.D(ram_1_dout[5]), .clk(and_21_out), .Q(d_ff_18_q));  // open: Qn, preset, reset
  D_Flip_Flop d_ff_19 (.D(ram_1_dout[6]), .clk(and_21_out), .Q(d_ff_19_q));  // open: Qn, preset, reset
  D_Flip_Flop d_ff_20 (.D(ram_1_dout[7]), .clk(and_21_out), .Q(d_ff_20_q));  // open: Qn, preset, reset
  D_Flip_Flop d_ff_21 (.D(ram_1_dout[0]), .clk(and_21_out), .Q(d_ff_21_q[0]));  // open: Qn, preset, reset
  D_Flip_Flop d_ff_22 (.D(ram_1_dout[1]), .clk(and_21_out), .Q(d_ff_21_q[1]));  // open: Qn, preset, reset
  D_Flip_Flop d_ff_23 (.D(ram_1_dout[2]), .clk(and_21_out), .Q(d_ff_21_q[2]));  // open: Qn, preset, reset
  D_Flip_Flop d_ff_24 (.D(ram_1_dout[3]), .clk(and_21_out), .Q(d_ff_21_q[3]));  // open: Qn, preset, reset
  or or_26 (or_36_out[6], and_43_out, and_63_out);
  or or_27 (or_36_out[5], and_44_out, and_64_out);
  and and_43 (and_43_out, or_20_out, d_ff_9_q[2]);
  and and_44 (and_44_out, or_20_out, d_ff_9_q[1]);
  and and_45 (and_45_out, ram_1_dout[0], or_20_out);
  and and_46 (and_46_out, ram_1_dout[1], or_20_out);
  and and_47 (and_47_out, ram_1_dout[2], or_20_out);
  and and_48 (and_48_out, ram_1_dout[3], or_20_out);
  and and_49 (and_49_out, d_ff_7_q[0], not_11_out);
  and and_50 (and_50_out, d_ff_7_q[1], not_11_out);
  and and_51 (and_51_out, d_ff_7_q[2], not_11_out);
  and and_52 (and_52_out, d_ff_7_q[3], not_11_out);
  not not_11 (not_11_out, fetch);
  and and_53 (and_53_out, d_ff_21_q[0], fetch);
  and and_54 (and_54_out, d_ff_21_q[1], fetch);
  and and_55 (and_55_out, d_ff_21_q[2], fetch);
  and and_56 (and_56_out, d_ff_21_q[3], fetch);
  or or_28 (or_36_out[4], and_57_out, and_65_out);
  or or_29 (or_36_out[3], and_58_out, and_66_out);
  and and_57 (and_57_out, or_20_out, d_ff_9_q[0]);
  and and_58 (and_58_out, or_20_out, or_30_out[3]);
  or or_30 (or_30_out[0], and_45_out, and_38_out);
  or or_31 (or_30_out[1], and_46_out, and_39_out);
  or or_32 (or_30_out[2], and_47_out, and_40_out);
  or or_33 (or_30_out[3], and_48_out, and_41_out);
  or or_34 (or_36_out[2], and_59_out, and_67_out);
  or or_35 (or_36_out[1], and_60_out, and_68_out);
  and and_59 (and_59_out, or_20_out, or_30_out[2]);
  and and_60 (and_60_out, or_20_out, or_30_out[1]);
  not not_12 (not_12_out, d_ff_20_q);
  or or_36 (or_36_out[0], and_61_out, and_79_out);
  and and_61 (and_61_out, or_20_out, or_30_out[0]);
  and and_62 (and_62_out, or_19_out, or_30_out[3]);
  not not_13 (not_13_out, d_ff_19_q);
  and and_63 (and_63_out, or_19_out, or_30_out[2]);
  and and_64 (and_64_out, or_19_out, or_30_out[1]);
  not not_14 (not_14_out, d_ff_18_q);
  not not_15 (not_15_out, d_ff_17_q);
  and and_65 (and_65_out, or_19_out, or_30_out[0]);
  and and_66 (and_66_out, or_19_out, d_ff_9_q[3]);
  and and_67 (and_67_out, or_19_out, d_ff_9_q[2]);
  and and_68 (and_68_out, or_19_out, d_ff_9_q[1]);
  and and_69 (and_69_out, d_ff_17_q, not_14_out, execute_puls_out, not_13_out, not_12_out);
  and and_70 (and_70_out, not_15_out, d_ff_18_q, execute_puls_out, not_13_out, not_12_out);
  and and_71 (and_71_out, d_ff_17_q, d_ff_18_q, execute_puls_out, not_13_out, not_12_out);
  and and_72 (_0100, not_15_out, not_14_out, execute_puls_out, d_ff_19_q, not_12_out);
  and and_73 (_0101, d_ff_17_q, not_14_out, execute_puls_out, d_ff_19_q, not_12_out);
  and and_74 (_0110, not_15_out, d_ff_18_q, execute_puls_out, d_ff_19_q, not_12_out);
  and and_75 (_0111, d_ff_17_q, d_ff_18_q, execute_puls_out, d_ff_19_q, not_12_out);
  and and_76 (_1000, not_15_out, not_14_out, execute_puls_out, not_13_out, d_ff_20_q);
  and and_77 (_1001, d_ff_17_q, not_14_out, execute_puls_out, not_13_out, d_ff_20_q);
  and and_78 (_1010, not_15_out, d_ff_18_q, execute_puls_out, not_13_out, d_ff_20_q);
  adder adder_5 (.a(or_30_out[1]), .b(adder_6_x), .x(adder_5_x), .y(adder_5_y));
  adder adder_6 (.a(d_ff_9_q[1]), .b(adder_7_x), .x(adder_6_x), .y(adder_6_y));
  adder adder_7 (.a(or_30_out[0]), .b(d_ff_9_q[0]), .x(adder_7_x), .y(adder_7_y[0]));
  and and_79 (and_79_out, or_19_out, d_ff_9_q[0]);
  adder adder_8 (.a(or_30_out[3]), .b(adder_9_x), .x(adder_8_x), .y(adder_8_y));
  or or_37 (adder_7_y[3], adder_8_y, adder_9_y);
  adder adder_9 (.a(d_ff_9_q[3]), .b(adder_10_x), .x(adder_9_x), .y(adder_9_y));
  adder adder_10 (.a(or_30_out[2]), .b(adder_11_x), .x(adder_10_x), .y(adder_10_y));
  or or_38 (adder_7_y[2], adder_10_y, adder_11_y);
  adder adder_11 (.a(d_ff_9_q[2]), .b(adder_5_x), .x(adder_11_x), .y(adder_11_y));
  or or_39 (adder_7_y[1], adder_5_y, adder_6_y);
  D_Flip_Flop d_ff_25 (.D(adder_8_x), .clk(and_71_out));  // open: Q, Qn, preset, reset

  // Notes on the sheet:
  //   fetch register
  //   write signal
  //   ram page
  //   program page
  //   enable write to a register
  //   delay write signal 
  //   a register
  //   ram side register
  //   opcode
  //   operand
  //   Instruction register
  //   store a register
  //   use Operand as address
  //   instruction decoder
  //   NOP
  //   LDA
  //   STA
  //   ADD
endmodule

module adder (
  input  a,
  input  b,
  output x,
  output y
);

  wire and_2_out, and_3_out, not_1_out, not_2_out;

  not not_1 (not_1_out, a);
  not not_2 (not_2_out, b);
  and and_1 (x, a, b);
  and and_2 (and_2_out, a, not_2_out);
  and and_3 (and_3_out, not_1_out, b);
  or or_1 (y, and_2_out, and_3_out);
endmodule
